// Logisim project Basic Computer Simulation.circ as structural Verilog: 3 circuits, main circuit main
// PC
module main (
  input  in_1,
  input  in_2,
  output out_3,
  output out_4
);

  wire clock_1_out, control_1_ac_load, control_1_address_multiplexer, control_1_ar_load, control_1_dr_load,
       control_1_ir_load, control_1_memory_read, control_1_memory_write, control_1_pc_clear,
       control_1_pc_increment, control_1_pc_load;
  wire [2:0] control_1_alu, control_1_select_lines_bardo;
  wire [5:0] AR_q, bit_extender_1_out, control_1_address, multiplexer_1_out;
  wire [15:0] AC_q, alu_1_alu_output, bit_extender_2_out, DR_q, IR_q, multiplexer_2_out, PC_q, ram_1_data,
       TR_q;

  Clock clock_1 (.out(clock_1_out));
  Control control_1 (
    .in_1(IR_q), .AC(AC_q), .Address(control_1_address), .Address_Multiplexer(control_1_address_multiplexer),
    .Memory_Read(control_1_memory_read), .DR_Load(control_1_dr_load),
    .Select_Lines_bardo(control_1_select_lines_bardo), .Memory_Write(control_1_memory_write),
    .AR_Load(control_1_ar_load), .PC_Load(control_1_pc_load), .PC_Clear(control_1_pc_clear),
    .ALU(control_1_alu), .AC_Load(control_1_ac_load), .IR_Load(control_1_ir_load),
    .PC_increment(control_1_pc_increment), .CLOCK(clock_1_out));
  Bit_Extender #(.in_width(16), .out_width(6)) bit_extender_1 (.in(multiplexer_2_out), .out(bit_extender_1_out));
  Register #(.width(16)) AC (.D(alu_1_alu_output), .en(control_1_ac_load), .Q(AC_q), .clk(clock_1_out));  // open: clr
  Register #(.width(16)) DR (.D(multiplexer_2_out), .en(control_1_dr_load), .Q(DR_q), .clk(clock_1_out));  // open: clr
  Multiplexer #(.width(6), .enable("false")) multiplexer_1 (
    .in0(bit_extender_1_out), .in1(control_1_address), .out(multiplexer_1_out),
    .sel(control_1_address_multiplexer));
  Register #(.width(16)) TR (.D(multiplexer_2_out), .Q(TR_q), .clk(clock_1_out));  // open: en, clr
  Counter #(.width(16), .max('hffff)) PC (
    .load(control_1_pc_load), .D(multiplexer_2_out), .count(control_1_pc_increment), .Q(PC_q),
    .clk(clock_1_out), .clr(control_1_pc_clear));  // open: carry
  Register #(.width(16)) IR (.D(multiplexer_2_out), .en(control_1_ir_load), .Q(IR_q), .clk(clock_1_out));  // open: clr
  RAM #(.addrWidth(6), .dataWidth(16), .bus("separate")) ram_1 (
    .addr(AR_q), .din(multiplexer_2_out), .data(ram_1_data), .str(control_1_memory_write), .clk(clock_1_out),
    .ld(control_1_memory_read));  // open: sel, clr
  ALU alu_1 (
    .in_1(in_1), .Input_1__AC(AC_q), .Input_2__DR(DR_q), .in_4(in_2), .Selection_of_ALU(control_1_alu),
    .out_6(out_3), .out_7(out_4), .ALU_Output(alu_1_alu_output));
  Register #(.width(6)) AR (.D(multiplexer_1_out), .en(control_1_ar_load), .Q(AR_q), .clk(clock_1_out));  // open: clr
  assign bit_extender_2_out = {{10{1'b0}}, AR_q};  // Bit_Extender bit_extender_2
  Multiplexer #(.select(3), .width(16), .enable("false")) multiplexer_2 (
    .in0(AC_q), .in1(DR_q), .in2(TR_q), .in3(bit_extender_2_out), .in4(ram_1_data), .in5(PC_q), .in6(IR_q),
    .out(multiplexer_2_out), .sel(control_1_select_lines_bardo));  // open: in7
endmodule

module ALU (
  input  in_1,
  input  [15:0] Input_1__AC,
  input  [15:0] Input_2__DR,
  input  in_4,
  input  [2:0] Selection_of_ALU,
  output out_6,
  output out_7,
  output [15:0] ALU_Output
);

  wire [15:0] adder_1_out, and_1_out, Complement_AC__DR_is_also_correct_out, or_1_out, subtractor_1_out,
       xor_1_out;

  Adder #(.width(16)) adder_1 (.a(Input_1__AC), .b(Input_2__DR), .out(adder_1_out), .cin(in_1), .cout(out_6));
  Subtractor #(.width(16)) subtractor_1 (
    .a(Input_1__AC), .b(Input_2__DR), .out(subtractor_1_out), .bin(in_4), .bout(out_7));
  assign and_1_out = Input_1__AC & Input_2__DR;  // AND_Gate and_1, 16 bits wide
  assign or_1_out = Input_1__AC | Input_2__DR;  // OR_Gate or_1, 16 bits wide
  assign xor_1_out = Input_1__AC ^ Input_2__DR;  // XOR_Gate xor_1, 16 bits wide
  assign Complement_AC__DR_is_also_correct_out = ~Input_1__AC;  // NOT_Gate Complement_AC__DR_is_also_correct, 16 bits wide
  Multiplexer #(.select(3), .width(16), .enable("false")) multiplexer_1 (
    .in0(adder_1_out), .in1(subtractor_1_out), .in2(Input_2__DR), .in3(and_1_out), .in4(or_1_out),
    .in5(xor_1_out), .in6(Complement_AC__DR_is_also_correct_out), .out(ALU_Output), .sel(Selection_of_ALU));  // open: in7
endmodule

module Control (
  input  [15:0] in_1,
  input  CLOCK,
  input  [15:0] AC,
  output [5:0] Address,
  output Address_Multiplexer,
  output Memory_Read,
  output DR_Load,
  output [2:0] Select_Lines_bardo,
  output Memory_Write,
  output AR_Load,
  output PC_Load,
  output PC_Clear,
  output [2:0] ALU,
  output AC_Load,
  output IR_Load,
  output PC_increment
);

  wire and_1_out, and_2_out, and_3_out, and_4_out, and_5_out, and_6_out, and_7_out, and_12_out, and_13_out,
       d_ff_1_q, decoder_1_out0, decoder_1_out1, decoder_1_out2, decoder_1_out3, decoder_1_out4,
       decoder_1_out5, decoder_1_out7, decoder_2_out0, decoder_2_out3, decoder_2_out4, decoder_2_out5,
       not_1_out, or_1_out, or_4_out;
  wire [3:0] SC_q;

  Counter #(.width(4), .max('hf)) SC (.Q(SC_q), .clk(CLOCK), .clr(d_ff_1_q));  // open: load, D, count, carry
  Decoder #(.select(3), .enable("false")) decoder_1 (
    .out0(decoder_1_out0), .out1(decoder_1_out1), .out2(decoder_1_out2), .out3(decoder_1_out3),
    .out4(decoder_1_out4), .out5(decoder_1_out5), .out7(decoder_1_out7), .sel(in_1[14:12]));  // open: out6
  Decoder #(.select(4), .enable("false")) decoder_2 (
    .out0(decoder_2_out0), .out1(IR_Load), .out2(Address_Multiplexer), .out3(decoder_2_out3),
    .out4(decoder_2_out4), .out5(decoder_2_out5), .sel(SC_q));  // open: out6, out7, out8, out9, out10, out11, out12, out13, out14, out15
  and and_1 (and_1_out, decoder_1_out0, decoder_2_out4);
  and and_2 (and_2_out, decoder_1_out0, decoder_2_out5);
  or or_1 (or_1_out, AC[0], AC[1], AC[2], AC[3], AC[4], AC[5], AC[6], AC[7], AC[8], AC[9], AC[10], AC[11], AC[12], AC[13], AC[14], AC[15]);
  and and_3 (and_3_out, decoder_1_out1, decoder_2_out4);
  and and_4 (and_4_out, decoder_1_out1, decoder_2_out5);
  and and_5 (and_5_out, decoder_1_out2, decoder_2_out4);
  and and_6 (and_6_out, decoder_1_out2, decoder_2_out5);
  not not_1 (not_1_out, or_1_out);
  and and_7 (and_7_out, decoder_2_out4, decoder_1_out7, not_1_out);
  and and_8 (Memory_Write, decoder_1_out3, decoder_2_out4);
  // AND_Gate and_9 has open pins: in0=decoder_1_out3, in1=decoder_2_out5, out=open
  or or_2 (PC_increment, IR_Load, and_7_out);
  and and_10 (PC_Clear, decoder_1_out4, decoder_2_out4);
  and and_11 (PC_Load, decoder_1_out4, decoder_2_out5);
  and and_12 (and_12_out, decoder_1_out5, decoder_2_out4);
  and and_13 (and_13_out, decoder_1_out5, decoder_2_out5);
  or or_3 (DR_Load, and_1_out, and_3_out, and_5_out, and_12_out);
  or or_4 (or_4_out, and_13_out, PC_Load, Memory_Write, and_7_out, and_6_out, and_4_out, and_2_out);
  D_Flip_Flop d_ff_1 (.clk(CLOCK), .D(or_4_out), .Q(d_ff_1_q), .en(1'b1));  // open: Qn, preset, reset
  or or_5 (AR_Load, Address_Multiplexer, decoder_2_out0);
  or or_6 (AC_Load, and_2_out, and_4_out, and_6_out, and_13_out);
  Priority_Encoder priority_encoder_1 (
    .in0(and_4_out), .in1(and_13_out), .in2(and_6_out), .in3(and_2_out), .out(ALU));  // open: in4, in5, in6, in7, en_in, gs, en_out
  or DR_LDA_OR_T1 (Memory_Read, DR_Load, IR_Load);
  Priority_Encoder priority_encoder_2 (
    .in0(Memory_Write), .in1(and_6_out), .in3(PC_Load), .in4(Memory_Read), .in5(AR_Load),
    .out(Select_Lines_bardo));  // open: in2, in6, in7, en_in, gs, en_out

  assign Address = in_1[5:0];

  // Notes on the sheet:
  //   D0 AND T4
  //   D0 AND T5
  //   D1 AND T4
  //   D1 AND T5
  //   D2 AND T4
  //   D2 AND T5
  //   D3 AND T4
  //   D3 AND T5
  //   (AC == 0) OR T1
  //   D4 AND T4
  //   D4 AND T5
  //   D5 AND T4
  //   D5 AND T5
  //   Address
  //   DR Load
  //   D0T5 + D1t5 +D2T5+D3+T4+D4T4+D5T5
  //   ALU Select Lines
  //   Select Lines
endmodule
